# Fritzing sketch dht11_lcd (saved by Fritzing 0.9.3b)
perfboards: 1
breadboards: 1

parts:
  DHT1 = DHT11 Humitidy and Temperature Sensor  # not connected
  Part1 = Arduino Uno (Rev3)
  R1 = Resistor [tolerance=±5% resistance=220 package=THT]
  LCD1 = LCD screen
  R2 = Rotary Potentiometer (Large) [package=THT]

nets:
  N1: Part1.D11_PWM/MOSI, LCD1.E
  N2: Part1.D12/MISO, LCD1.RS
  N3: Part1.D2, LCD1.DB7
  N4: Part1.D3_PWM, LCD1.DB6
  N5: Part1.D4, LCD1.DB5
  N6: Part1.D5_PWM, LCD1.DB4
  N7: Part1.D7, R1.Pin_0
  5V: Part1.5V, R1.Pin_1, LCD1.VDD, LCD1.LED+, R2.leg2
  N8: LCD1.VSS, LCD1.R/W, LCD1.LED-, R2.leg1
  N9: LCD1.V0, R2.wiper

custom parts:
  DHT11 Humitidy and Temperature Sensor: DHT11 Humidity and Temperature Sensor
