# Fritzing sketch dht11_simple (saved by Fritzing 0.9.3b)
perfboards: 1
breadboards: 1

parts:
  DHT1 = DHT11 Humitidy and Temperature Sensor  # not connected
  Part1 = Arduino Uno (Rev3)
  R1 = Resistor [tolerance=±5% resistance=220 package=THT]

nets:
  N1: Part1.D2, R1.Pin_0
  N2: Part1.5V, R1.Pin_1

custom parts:
  DHT11 Humitidy and Temperature Sensor: DHT11 Humidity and Temperature Sensor
